// Logisim project RV32I.circ as structural Verilog: 1 circuit, main circuit main
module main (
  input  reset
);

  wire clk, decoder_1_out0, decoder_1_out1, decoder_1_out2, decoder_1_out3, decoder_1_out4, decoder_1_out5,
       or_1_out;
  wire [2:0] instructiondecoder_1_funct3, instructiondecoder_1_type;
  wire [4:0] instructiondecoder_1_rd, instructiondecoder_1_rs1, instructiondecoder_1_rs2;
  wire [6:0] instructiondecoder_1_funct7;
  wire [31:0] adder_1_out, instructiondecoder_1_bimm, instructiondecoder_1_iimm, instructiondecoder_1_jimm,
       instructiondecoder_1_simm, instructiondecoder_1_uimm, main_1_data_out, main_2_rs1, main_2_rs2,
       main_3_d, main_4_data_out, multiplexer_1_out, multiplexer_2_out, PC_q;

  Adder #(.width(32)) adder_1 (.a(PC_q), .b(32'h1), .out(adder_1_out));  // open: cin, cout
  Clock Clock (.out(clk));
  Multiplexer #(.enable("false"), .width(32)) multiplexer_1 (
    .in0(adder_1_out), .out(multiplexer_1_out), .sel(1'b0));  // open: in1
  Register #(.width(32)) PC (.D(multiplexer_1_out), .Q(PC_q), .clk(clk), .clr(reset));  // open: en
  // Probe on PC_q
  InstructionMemory_main main_1 (.data_out(main_1_data_out));  // open: address
  // Probe on main_1_data_out
  // Probe on instructiondecoder_1_type
  InstructionDecoder instructiondecoder_1 (
    .rd(instructiondecoder_1_rd), .funct3(instructiondecoder_1_funct3), .rs1(instructiondecoder_1_rs1),
    .rs2(instructiondecoder_1_rs2), .funct7(instructiondecoder_1_funct7), .\type (instructiondecoder_1_type),
    .IImm(instructiondecoder_1_iimm), .SImm(instructiondecoder_1_simm), .BImm(instructiondecoder_1_bimm),
    .UImm(instructiondecoder_1_uimm), .JImm(instructiondecoder_1_jimm), .Instruction(main_1_data_out));
  // Probe on instructiondecoder_1_rd
  // Probe on instructiondecoder_1_funct3
  // Probe on instructiondecoder_1_rs1
  // Probe on instructiondecoder_1_rs2
  // Probe on instructiondecoder_1_funct7
  // Probe on instructiondecoder_1_iimm
  // Probe on instructiondecoder_1_simm
  // Probe on instructiondecoder_1_bimm
  // Probe on instructiondecoder_1_uimm
  // Probe on instructiondecoder_1_jimm
  Decoder #(.select(3)) decoder_1 (
    .out0(decoder_1_out0), .out1(decoder_1_out1), .out2(decoder_1_out2), .out3(decoder_1_out3),
    .out4(decoder_1_out4), .out5(decoder_1_out5), .sel(instructiondecoder_1_type));  // open: out6, out7, en
  // Probe on instructiondecoder_1_rs1
  or or_1 (or_1_out, decoder_1_out0, decoder_1_out1);
  RegFile_main main_2 (
    .rs1(main_2_rs1), .rs2(main_2_rs2), .sel_rs1(instructiondecoder_1_rs1),
    .sel_rs2(instructiondecoder_1_rs2), .write(or_1_out), .rd(instructiondecoder_1_rd), .rst(reset),
    .data(main_3_d), .clk(clk));
  // Probe on main_2_rs1
  // Probe on main_2_rs2
  Multiplexer #(.enable("false"), .width(32)) multiplexer_2 (
    .in0(main_2_rs2), .in1(instructiondecoder_1_iimm), .out(multiplexer_2_out), .sel(decoder_1_out1));
  // Probe on main_3_d
  ALU_main main_3 (
    .d(main_3_d), .s1(main_2_rs1), .s2(multiplexer_2_out), .funct7(instructiondecoder_1_funct7),
    .funct3(instructiondecoder_1_funct3));
  DataMemory_main main_4 (.data_out(main_4_data_out));  // open: address, byte_writes, clk, data_in

  // Other names for the same wires on the sheet: rst = reset

  // Notes on the sheet:
  //   Add 1 because IMem 
  //   is accessible only in 
  //   multiples of 4 bytes 
  //   (since all instructions 
  //   are 32bits exactly)
endmodule
